// Logisim project signed_pipelined_8bit_mul.circ as structural Verilog
module and_add1 (
  input  Cin,
  input  A,
  input  B,
  input  C,
  output Z,
  output Cout
);

  wire and_1_out;

  and and_1 (and_1_out, A, B);
  Adder #(.width(1)) adder_1 (.a(and_1_out), .b(C), .out(Z), .cin(Cin), .cout(Cout));
endmodule

module cpa (
  input  [7:0] A,
  input  [6:0] B,
  output [7:0] Z,
  output Cout
);

  wire adder_1_cout, adder_2_cout, adder_3_cout, adder_4_cout, adder_5_cout, adder_6_cout, adder_7_cout;

  Adder #(.width(1)) adder_1 (.a(A[0]), .b(B[0]), .out(Z[0]), .cout(adder_1_cout));  // open: cin
  Adder #(.width(1)) adder_2 (.a(A[1]), .b(B[1]), .out(Z[1]), .cin(adder_1_cout), .cout(adder_2_cout));
  Adder #(.width(1)) adder_3 (.a(A[2]), .b(B[2]), .out(Z[2]), .cin(adder_2_cout), .cout(adder_3_cout));
  Adder #(.width(1)) adder_4 (.a(A[3]), .b(B[3]), .out(Z[3]), .cin(adder_3_cout), .cout(adder_4_cout));
  Adder #(.width(1)) adder_5 (.a(A[4]), .b(B[4]), .out(Z[4]), .cin(adder_4_cout), .cout(adder_5_cout));
  Adder #(.width(1)) adder_6 (.a(A[5]), .b(B[5]), .out(Z[5]), .cin(adder_5_cout), .cout(adder_6_cout));
  Adder #(.width(1)) adder_7 (.a(A[6]), .b(B[6]), .out(Z[6]), .cin(adder_6_cout), .cout(adder_7_cout));
  Adder #(.width(1)) adder_8 (.a(A[7]), .b(1'b1), .out(Z[7]), .cin(adder_7_cout), .cout(Cout));
endmodule

module signed_pipeline_mul8 (
  input  [7:0] A,
  input  [7:0] B,
  output [15:0] Z,
  output Cout
);

  wire clock_1_out;
  wire [3:0] csa_signed_1_z;
  wire [6:0] csa_signed_1_znext, csa_signed_2_znext, csa_signed_3_znext, csa_signed_4_znext,
       csa_signed_5_znext, csa_signed_6_znext, csa_signed_7_znext, csa_signed_invert_1_znext, register_4_q,
       register_7_q;
  wire [7:0] csa_signed_1_cout, csa_signed_2_cout, csa_signed_3_cout, csa_signed_4_cout, csa_signed_5_cout,
       csa_signed_6_cout, csa_signed_7_cout, csa_signed_invert_1_cout, register_1_q, register_2_q,
       register_3_q, register_5_q, register_6_q;

  Clock clock_1 (.out(clock_1_out));
  csa_signed csa_signed_1 (
    .Cin({8{1'b0}}), .A(A), .B(B[0]), .C({7{1'b0}}), .Const(1'b0), .Cout(csa_signed_1_cout),
    .Z(csa_signed_1_z[0]), .Znext(csa_signed_1_znext));
  csa_signed csa_signed_2 (
    .Cin(csa_signed_1_cout), .A(A), .B(B[1]), .C(csa_signed_1_znext), .Const(1'b1), .Cout(csa_signed_2_cout),
    .Z(csa_signed_1_z[1]), .Znext(csa_signed_2_znext));
  csa_signed csa_signed_3 (
    .Cin(csa_signed_2_cout), .A(A), .B(B[2]), .C(csa_signed_2_znext), .Const(1'b0), .Cout(csa_signed_3_cout),
    .Z(csa_signed_1_z[2]), .Znext(csa_signed_3_znext));
  csa_signed csa_signed_4 (
    .Cin(csa_signed_3_cout), .A(A), .B(B[3]), .C(csa_signed_3_znext), .Const(1'b0), .Cout(csa_signed_4_cout),
    .Z(csa_signed_1_z[3]), .Znext(csa_signed_4_znext));
  Register register_1 (.D(A), .Q(register_1_q), .clk(clock_1_out));  // open: en, clr
  Register register_2 (.D(B), .Q(register_2_q), .clk(clock_1_out));  // open: en, clr
  Register register_3 (.D(csa_signed_4_cout), .Q(register_3_q), .clk(clock_1_out));  // open: en, clr
  Register #(.width(7)) register_4 (.D(csa_signed_4_znext), .Q(register_4_q), .clk(clock_1_out));  // open: en, clr
  Register #(.width(4)) register_5 (.D(csa_signed_1_z), .Q(register_5_q[3:0]), .clk(clock_1_out));  // open: en, clr
  csa_signed csa_signed_5 (
    .Cin(register_3_q), .A(register_1_q), .B(register_2_q[4]), .C(register_4_q), .Const(1'b0),
    .Cout(csa_signed_5_cout), .Z(register_5_q[4]), .Znext(csa_signed_5_znext));
  csa_signed csa_signed_6 (
    .Cin(csa_signed_5_cout), .A(register_1_q), .B(register_2_q[5]), .C(csa_signed_5_znext), .Const(1'b0),
    .Cout(csa_signed_6_cout), .Z(register_5_q[5]), .Znext(csa_signed_6_znext));
  csa_signed csa_signed_7 (
    .Cin(csa_signed_6_cout), .A(register_1_q), .B(register_2_q[6]), .C(csa_signed_6_znext), .Const(1'b0),
    .Cout(csa_signed_7_cout), .Z(register_5_q[6]), .Znext(csa_signed_7_znext));
  Register register_6 (.D(csa_signed_invert_1_cout), .Q(register_6_q), .clk(clock_1_out));  // open: en, clr
  csa_signed_invert csa_signed_invert_1 (
    .Cin(csa_signed_7_cout), .A(register_1_q), .B(register_2_q[7]), .C(csa_signed_7_znext), .Const(1'b0),
    .Cout(csa_signed_invert_1_cout), .Z(register_5_q[7]), .Znext(csa_signed_invert_1_znext));
  Register #(.width(7)) register_7 (
    .D(csa_signed_invert_1_znext), .Q(register_7_q), .clk(clock_1_out));  // open: en, clr
  Register register_8 (.D(register_5_q), .Q(Z[7:0]), .clk(clock_1_out));  // open: en, clr
  cpa cpa_1 (.A(register_6_q), .B(register_7_q), .Z(Z[15:8]), .Cout(Cout));
endmodule

module csa_signed (
  input  [7:0] Cin,
  input  [7:0] A,
  input  B,
  input  [6:0] C,
  input  Const,
  output [7:0] Cout,
  output Z,
  output [6:0] Znext
);

  and_add1 and_add1_1 (.Cin(Cin[0]), .A(A[0]), .B(B), .C(C[0]), .Z(Z), .Cout(Cout[0]));
  and_add1 and_add1_2 (.Cin(Cin[1]), .A(A[1]), .B(B), .C(C[1]), .Z(Znext[0]), .Cout(Cout[1]));
  and_add1 and_add1_3 (.Cin(Cin[2]), .A(A[2]), .B(B), .C(C[2]), .Z(Znext[1]), .Cout(Cout[2]));
  and_add1 and_add1_4 (.Cin(Cin[3]), .A(A[3]), .B(B), .C(C[3]), .Z(Znext[2]), .Cout(Cout[3]));
  and_add1 and_add1_5 (.Cin(Cin[4]), .A(A[4]), .B(B), .C(C[4]), .Z(Znext[3]), .Cout(Cout[4]));
  and_add1 and_add1_6 (.Cin(Cin[5]), .A(A[5]), .B(B), .C(C[5]), .Z(Znext[4]), .Cout(Cout[5]));
  and_add1 and_add1_7 (.Cin(Cin[6]), .A(A[6]), .B(B), .C(C[6]), .Z(Znext[5]), .Cout(Cout[6]));
  nan_add1 nan_add1_1 (.Cin(Cin[7]), .A(A[7]), .B(B), .C(Const), .Z(Znext[6]), .Cout(Cout[7]));
endmodule

module nan_add1 (
  input  Cin,
  input  A,
  input  B,
  input  C,
  output Z,
  output Cout
);

  wire nand_1_out;

  nand nand_1 (nand_1_out, A, B);
  Adder #(.width(1)) adder_1 (.a(nand_1_out), .b(C), .out(Z), .cin(Cin), .cout(Cout));
endmodule

module csa_signed_invert (
  input  [7:0] Cin,
  input  [7:0] A,
  input  B,
  input  [6:0] C,
  input  Const,
  output [7:0] Cout,
  output Z,
  output [6:0] Znext
);

  nan_add1 nan_add1_1 (.Cin(Cin[0]), .A(A[0]), .B(B), .C(C[0]), .Z(Z), .Cout(Cout[0]));
  nan_add1 nan_add1_2 (.Cin(Cin[1]), .A(A[1]), .B(B), .C(C[1]), .Z(Znext[0]), .Cout(Cout[1]));
  nan_add1 nan_add1_3 (.Cin(Cin[2]), .A(A[2]), .B(B), .C(C[2]), .Z(Znext[1]), .Cout(Cout[2]));
  nan_add1 nan_add1_4 (.Cin(Cin[3]), .A(A[3]), .B(B), .C(C[3]), .Z(Znext[2]), .Cout(Cout[3]));
  nan_add1 nan_add1_5 (.Cin(Cin[4]), .A(A[4]), .B(B), .C(C[4]), .Z(Znext[3]), .Cout(Cout[4]));
  nan_add1 nan_add1_6 (.Cin(Cin[5]), .A(A[5]), .B(B), .C(C[5]), .Z(Znext[4]), .Cout(Cout[5]));
  nan_add1 nan_add1_7 (.Cin(Cin[6]), .A(A[6]), .B(B), .C(C[6]), .Z(Znext[5]), .Cout(Cout[6]));
  and_add1 and_add1_1 (.Cin(Cin[7]), .A(A[7]), .B(B), .C(Const), .Z(Znext[6]), .Cout(Cout[7]));
endmodule
