// Logisim project unsigned_8bit_mul.circ as structural Verilog
module add1 (
  input  Cin,
  input  A,
  input  B,
  input  C,
  output Z,
  output Cout
);

  wire and_1_out;

  and and_1 (and_1_out, A, B);
  Adder #(.width(1)) adder_1 (.a(and_1_out), .b(C), .out(Z), .cin(Cin), .cout(Cout));
endmodule

module add4 (
  input  [3:0] C,
  input  [3:0] A,
  input  B,
  input  [3:0] C_2,
  output [3:0] Cout,
  output [3:0] Z
);

  add1 add1_1 (.Cin(C[0]), .A(A[0]), .B(B), .C(C_2[0]), .Z(Z[0]), .Cout(Cout[0]));
  add1 add1_2 (.Cin(C[1]), .A(A[1]), .B(B), .C(C_2[1]), .Z(Z[1]), .Cout(Cout[1]));
  add1 add1_3 (.Cin(C[2]), .A(A[2]), .B(B), .C(C_2[2]), .Z(Z[2]), .Cout(Cout[2]));
  add1 add1_4 (.Cin(C[3]), .A(A[3]), .B(B), .C(C_2[3]), .Z(Z[3]), .Cout(Cout[3]));
endmodule

module csa8 (
  input  [7:0] Cin,
  input  [7:0] A,
  input  B,
  input  [6:0] C,
  output [7:0] Cout,
  output Z,
  output [6:0] Znext
);

  add4 add4_1 (.C(Cin[3:0]), .A(A[3:0]), .B(B), .C_2(C[3:0]), .Cout(Cout[3:0]), .Z({Znext[2:0], Z}));
  add4 add4_2 (.C(Cin[7:4]), .A(A[7:4]), .B(B), .C_2({1'b0, C[6:4]}), .Cout(Cout[7:4]), .Z(Znext[6:3]));
endmodule

module mul8 (
  input  [7:0] A,
  input  [7:0] B,
  output [15:0] Z,
  output Cout
);

  wire [6:0] csa8_1_znext, csa8_2_znext, csa8_3_znext, csa8_4_znext, csa8_5_znext, csa8_6_znext,
       csa8_7_znext, csa8_8_znext;
  wire [7:0] csa8_1_cout, csa8_2_cout, csa8_3_cout, csa8_4_cout, csa8_5_cout, csa8_6_cout, csa8_7_cout,
       csa8_8_cout;

  csa8 csa8_1 (.Cin({8{1'b0}}), .A(A), .B(B[0]), .C({7{1'b0}}), .Cout(csa8_1_cout), .Z(Z[0]), .Znext(csa8_1_znext));
  csa8 csa8_2 (
    .Cin(csa8_1_cout), .A(A), .B(B[1]), .C(csa8_1_znext), .Cout(csa8_2_cout), .Z(Z[1]), .Znext(csa8_2_znext));
  csa8 csa8_3 (
    .Cin(csa8_2_cout), .A(A), .B(B[2]), .C(csa8_2_znext), .Cout(csa8_3_cout), .Z(Z[2]), .Znext(csa8_3_znext));
  csa8 csa8_4 (
    .Cin(csa8_3_cout), .A(A), .B(B[3]), .C(csa8_3_znext), .Cout(csa8_4_cout), .Z(Z[3]), .Znext(csa8_4_znext));
  csa8 csa8_5 (
    .Cin(csa8_4_cout), .A(A), .B(B[4]), .C(csa8_4_znext), .Cout(csa8_5_cout), .Z(Z[4]), .Znext(csa8_5_znext));
  csa8 csa8_6 (
    .Cin(csa8_5_cout), .A(A), .B(B[5]), .C(csa8_5_znext), .Cout(csa8_6_cout), .Z(Z[5]), .Znext(csa8_6_znext));
  csa8 csa8_7 (
    .Cin(csa8_6_cout), .A(A), .B(B[6]), .C(csa8_6_znext), .Cout(csa8_7_cout), .Z(Z[6]), .Znext(csa8_7_znext));
  csa8 csa8_8 (
    .Cin(csa8_7_cout), .A(A), .B(B[7]), .C(csa8_7_znext), .Cout(csa8_8_cout), .Z(Z[7]), .Znext(csa8_8_znext));
  cpa cpa_1 (.A(csa8_8_cout), .B(csa8_8_znext), .Z(Z[15:8]), .Cout(Cout));
endmodule

module cpa (
  input  [7:0] A,
  input  [6:0] B,
  output [7:0] Z,
  output Cout
);

  wire adder_1_cout, adder_2_cout, adder_3_cout, adder_4_cout, adder_5_cout, adder_6_cout, adder_7_cout;

  Adder #(.width(1)) adder_1 (.a(A[0]), .b(B[0]), .out(Z[0]), .cout(adder_1_cout));  // open: cin
  Adder #(.width(1)) adder_2 (.a(A[1]), .b(B[1]), .out(Z[1]), .cin(adder_1_cout), .cout(adder_2_cout));
  Adder #(.width(1)) adder_3 (.a(A[2]), .b(B[2]), .out(Z[2]), .cin(adder_2_cout), .cout(adder_3_cout));
  Adder #(.width(1)) adder_4 (.a(A[3]), .b(B[3]), .out(Z[3]), .cin(adder_3_cout), .cout(adder_4_cout));
  Adder #(.width(1)) adder_5 (.a(A[4]), .b(B[4]), .out(Z[4]), .cin(adder_4_cout), .cout(adder_5_cout));
  Adder #(.width(1)) adder_6 (.a(A[5]), .b(B[5]), .out(Z[5]), .cin(adder_5_cout), .cout(adder_6_cout));
  Adder #(.width(1)) adder_7 (.a(A[6]), .b(B[6]), .out(Z[6]), .cin(adder_6_cout), .cout(adder_7_cout));
  Adder #(.width(1)) adder_8 (.a(A[7]), .b(1'b0), .out(Z[7]), .cin(adder_7_cout), .cout(Cout));
endmodule
