// Logisim project unsigned_pipelined_8bit_mul.circ as structural Verilog
module add1 (
  input  Cin,
  input  A,
  input  B,
  input  C,
  output Z,
  output Cout
);

  wire and_1_out;

  and and_1 (and_1_out, A, B);
  Adder #(.width(1)) adder_1 (.a(and_1_out), .b(C), .out(Z), .cin(Cin), .cout(Cout));
endmodule

module add4 (
  input  [3:0] C,
  input  [3:0] A,
  input  B,
  input  [3:0] C_2,
  output [3:0] Cout,
  output [3:0] Z
);

  add1 add1_1 (.Cin(C[0]), .A(A[0]), .B(B), .C(C_2[0]), .Z(Z[0]), .Cout(Cout[0]));
  add1 add1_2 (.Cin(C[1]), .A(A[1]), .B(B), .C(C_2[1]), .Z(Z[1]), .Cout(Cout[1]));
  add1 add1_3 (.Cin(C[2]), .A(A[2]), .B(B), .C(C_2[2]), .Z(Z[2]), .Cout(Cout[2]));
  add1 add1_4 (.Cin(C[3]), .A(A[3]), .B(B), .C(C_2[3]), .Z(Z[3]), .Cout(Cout[3]));
endmodule

module csa8 (
  input  [7:0] Cin,
  input  [7:0] A,
  input  B,
  input  [6:0] C,
  output [7:0] Cout,
  output Z,
  output [6:0] Znext
);

  add4 add4_1 (.C(Cin[3:0]), .A(A[3:0]), .B(B), .C_2(C[3:0]), .Cout(Cout[3:0]), .Z({Znext[2:0], Z}));
  add4 add4_2 (.C(Cin[7:4]), .A(A[7:4]), .B(B), .C_2({1'b0, C[6:4]}), .Cout(Cout[7:4]), .Z(Znext[6:3]));
endmodule

module mul8 (
  input  [7:0] A,
  input  [7:0] B,
  output [15:0] Z,
  output Cout
);

  wire [6:0] csa8_1_znext, csa8_2_znext, csa8_3_znext, csa8_4_znext, csa8_5_znext, csa8_6_znext,
       csa8_7_znext, csa8_8_znext;
  wire [7:0] csa8_1_cout, csa8_2_cout, csa8_3_cout, csa8_4_cout, csa8_5_cout, csa8_6_cout, csa8_7_cout,
       csa8_8_cout;

  csa8 csa8_1 (.Cin({8{1'b0}}), .A(A), .B(B[0]), .C({7{1'b0}}), .Cout(csa8_1_cout), .Z(Z[0]), .Znext(csa8_1_znext));
  csa8 csa8_2 (
    .Cin(csa8_1_cout), .A(A), .B(B[1]), .C(csa8_1_znext), .Cout(csa8_2_cout), .Z(Z[1]), .Znext(csa8_2_znext));
  csa8 csa8_3 (
    .Cin(csa8_2_cout), .A(A), .B(B[2]), .C(csa8_2_znext), .Cout(csa8_3_cout), .Z(Z[2]), .Znext(csa8_3_znext));
  csa8 csa8_4 (
    .Cin(csa8_3_cout), .A(A), .B(B[3]), .C(csa8_3_znext), .Cout(csa8_4_cout), .Z(Z[3]), .Znext(csa8_4_znext));
  csa8 csa8_5 (
    .Cin(csa8_4_cout), .A(A), .B(B[4]), .C(csa8_4_znext), .Cout(csa8_5_cout), .Z(Z[4]), .Znext(csa8_5_znext));
  csa8 csa8_6 (
    .Cin(csa8_5_cout), .A(A), .B(B[5]), .C(csa8_5_znext), .Cout(csa8_6_cout), .Z(Z[5]), .Znext(csa8_6_znext));
  csa8 csa8_7 (
    .Cin(csa8_6_cout), .A(A), .B(B[6]), .C(csa8_6_znext), .Cout(csa8_7_cout), .Z(Z[6]), .Znext(csa8_7_znext));
  csa8 csa8_8 (
    .Cin(csa8_7_cout), .A(A), .B(B[7]), .C(csa8_7_znext), .Cout(csa8_8_cout), .Z(Z[7]), .Znext(csa8_8_znext));
  cpa cpa_1 (.A(csa8_8_cout), .B(csa8_8_znext), .Z(Z[15:8]), .Cout(Cout));
endmodule

module cpa (
  input  [7:0] A,
  input  [6:0] B,
  output [7:0] Z,
  output Cout
);

  wire adder_1_cout, adder_2_cout, adder_3_cout, adder_4_cout, adder_5_cout, adder_6_cout, adder_7_cout;

  Adder #(.width(1)) adder_1 (.a(A[0]), .b(B[0]), .out(Z[0]), .cout(adder_1_cout));  // open: cin
  Adder #(.width(1)) adder_2 (.a(A[1]), .b(B[1]), .out(Z[1]), .cin(adder_1_cout), .cout(adder_2_cout));
  Adder #(.width(1)) adder_3 (.a(A[2]), .b(B[2]), .out(Z[2]), .cin(adder_2_cout), .cout(adder_3_cout));
  Adder #(.width(1)) adder_4 (.a(A[3]), .b(B[3]), .out(Z[3]), .cin(adder_3_cout), .cout(adder_4_cout));
  Adder #(.width(1)) adder_5 (.a(A[4]), .b(B[4]), .out(Z[4]), .cin(adder_4_cout), .cout(adder_5_cout));
  Adder #(.width(1)) adder_6 (.a(A[5]), .b(B[5]), .out(Z[5]), .cin(adder_5_cout), .cout(adder_6_cout));
  Adder #(.width(1)) adder_7 (.a(A[6]), .b(B[6]), .out(Z[6]), .cin(adder_6_cout), .cout(adder_7_cout));
  Adder #(.width(1)) adder_8 (.a(A[7]), .b(1'b0), .out(Z[7]), .cin(adder_7_cout), .cout(Cout));
endmodule

module pipeline_mul8_8cycle (
  input  [7:0] A,
  input  [7:0] B,
  output [15:0] Z,
  output Cout
);

  wire clock_1_out, csa8_1_z;
  wire [1:0] register_5_q, register_10_q;
  wire [2:0] register_15_q;
  wire [2:2] csa8_3_z;
  wire [3:0] register_20_q;
  wire [3:3] csa8_4_z;
  wire [4:4] csa8_5_z;
  wire [5:0] register_25_q, register_30_q;
  wire [6:0] csa8_1_znext, csa8_2_znext, csa8_3_znext, csa8_4_znext, csa8_5_znext, csa8_6_znext,
       csa8_7_znext, csa8_8_znext, register_4_q, register_9_q, register_14_q, register_19_q, register_24_q,
       register_29_q, register_34_q, register_35_q, register_37_q;
  wire [6:6] csa8_7_z;
  wire [7:0] csa8_1_cout, csa8_2_cout, csa8_3_cout, csa8_4_cout, csa8_5_cout, csa8_6_cout, csa8_7_cout,
       csa8_8_cout, register_1_q, register_2_q, register_3_q, register_6_q, register_7_q, register_8_q,
       register_11_q, register_12_q, register_13_q, register_16_q, register_17_q, register_18_q,
       register_21_q, register_22_q, register_23_q, register_26_q, register_27_q, register_28_q,
       register_31_q, register_32_q, register_33_q, register_36_q;
  wire [7:7] csa8_8_z;

  Clock clock_1 (.out(clock_1_out));
  csa8 csa8_1 (.Cin({8{1'b0}}), .A(A), .B(B[0]), .C({7{1'b0}}), .Cout(csa8_1_cout), .Z(csa8_1_z), .Znext(csa8_1_znext));
  Register register_1 (.D(A), .Q(register_1_q), .clk(clock_1_out));  // open: en, clr
  Register register_2 (.D(B), .Q(register_2_q), .clk(clock_1_out));  // open: en, clr
  Register register_3 (.D(csa8_1_cout), .Q(register_3_q), .clk(clock_1_out));  // open: en, clr
  Register #(.width(7)) register_4 (.D(csa8_1_znext), .Q(register_4_q), .clk(clock_1_out));  // open: en, clr
  Register #(.width(1)) register_5 (.D(csa8_1_z), .Q(register_5_q[0]), .clk(clock_1_out));  // open: en, clr
  csa8 csa8_2 (
    .Cin(register_3_q), .A(register_1_q), .B(register_2_q[1]), .C(register_4_q), .Cout(csa8_2_cout),
    .Z(register_5_q[1]), .Znext(csa8_2_znext));
  Register register_6 (.D(register_1_q), .Q(register_6_q), .clk(clock_1_out));  // open: en, clr
  Register register_7 (.D(register_2_q), .Q(register_7_q), .clk(clock_1_out));  // open: en, clr
  Register register_8 (.D(csa8_2_cout), .Q(register_8_q), .clk(clock_1_out));  // open: en, clr
  Register #(.width(7)) register_9 (.D(csa8_2_znext), .Q(register_9_q), .clk(clock_1_out));  // open: en, clr
  Register #(.width(2)) register_10 (.D(register_5_q), .Q(register_10_q), .clk(clock_1_out));  // open: en, clr
  csa8 csa8_3 (
    .Cin(register_8_q), .A(register_6_q), .B(register_7_q[2]), .C(register_9_q), .Cout(csa8_3_cout),
    .Z(csa8_3_z[2]), .Znext(csa8_3_znext));
  Register register_11 (.D(register_6_q), .Q(register_11_q), .clk(clock_1_out));  // open: en, clr
  Register register_12 (.D(register_7_q), .Q(register_12_q), .clk(clock_1_out));  // open: en, clr
  Register register_13 (.D(csa8_3_cout), .Q(register_13_q), .clk(clock_1_out));  // open: en, clr
  Register #(.width(7)) register_14 (.D(csa8_3_znext), .Q(register_14_q), .clk(clock_1_out));  // open: en, clr
  Register #(.width(3)) register_15 (
    .D({csa8_3_z[2], register_10_q}), .Q(register_15_q), .clk(clock_1_out));  // open: en, clr
  csa8 csa8_4 (
    .Cin(register_13_q), .A(register_11_q), .B(register_12_q[3]), .C(register_14_q), .Cout(csa8_4_cout),
    .Z(csa8_4_z[3]), .Znext(csa8_4_znext));
  Register register_16 (.D(register_11_q), .Q(register_16_q), .clk(clock_1_out));  // open: en, clr
  Register register_17 (.D(register_12_q), .Q(register_17_q), .clk(clock_1_out));  // open: en, clr
  Register register_18 (.D(csa8_4_cout), .Q(register_18_q), .clk(clock_1_out));  // open: en, clr
  Register #(.width(7)) register_19 (.D(csa8_4_znext), .Q(register_19_q), .clk(clock_1_out));  // open: en, clr
  Register #(.width(4)) register_20 (
    .D({csa8_4_z[3], register_15_q}), .Q(register_20_q), .clk(clock_1_out));  // open: en, clr
  csa8 csa8_5 (
    .Cin(register_18_q), .A(register_16_q), .B(register_17_q[4]), .C(register_19_q), .Cout(csa8_5_cout),
    .Z(csa8_5_z[4]), .Znext(csa8_5_znext));
  Register register_21 (.D(register_16_q), .Q(register_21_q), .clk(clock_1_out));  // open: en, clr
  Register register_22 (.D(register_17_q), .Q(register_22_q), .clk(clock_1_out));  // open: en, clr
  Register register_23 (.D(csa8_5_cout), .Q(register_23_q), .clk(clock_1_out));  // open: en, clr
  Register #(.width(7)) register_24 (.D(csa8_5_znext), .Q(register_24_q), .clk(clock_1_out));  // open: en, clr
  Register #(.width(5)) register_25 (
    .D({csa8_5_z[4], register_20_q}), .Q(register_25_q[4:0]), .clk(clock_1_out));  // open: en, clr
  Register register_26 (.D(register_21_q), .Q(register_26_q), .clk(clock_1_out));  // open: en, clr
  Register register_27 (.D(register_22_q), .Q(register_27_q), .clk(clock_1_out));  // open: en, clr
  csa8 csa8_6 (
    .Cin(register_23_q), .A(register_21_q), .B(register_22_q[5]), .C(register_24_q), .Cout(csa8_6_cout),
    .Z(register_25_q[5]), .Znext(csa8_6_znext));
  Register register_28 (.D(csa8_6_cout), .Q(register_28_q), .clk(clock_1_out));  // open: en, clr
  Register #(.width(7)) register_29 (.D(csa8_6_znext), .Q(register_29_q), .clk(clock_1_out));  // open: en, clr
  Register #(.width(6)) register_30 (.D(register_25_q), .Q(register_30_q), .clk(clock_1_out));  // open: en, clr
  Register register_31 (.D(register_26_q), .Q(register_31_q), .clk(clock_1_out));  // open: en, clr
  Register register_32 (.D(register_27_q), .Q(register_32_q), .clk(clock_1_out));  // open: en, clr
  Register register_33 (.D(csa8_7_cout), .Q(register_33_q), .clk(clock_1_out));  // open: en, clr
  csa8 csa8_7 (
    .Cin(register_28_q), .A(register_26_q), .B(register_27_q[6]), .C(register_29_q), .Cout(csa8_7_cout),
    .Z(csa8_7_z[6]), .Znext(csa8_7_znext));
  Register #(.width(7)) register_34 (.D(csa8_7_znext), .Q(register_34_q), .clk(clock_1_out));  // open: en, clr
  Register #(.width(7)) register_35 (
    .D({csa8_7_z[6], register_30_q}), .Q(register_35_q), .clk(clock_1_out));  // open: en, clr
  Register register_36 (.D(csa8_8_cout), .Q(register_36_q), .clk(clock_1_out));  // open: en, clr
  csa8 csa8_8 (
    .Cin(register_33_q), .A(register_31_q), .B(register_32_q[7]), .C(register_34_q), .Cout(csa8_8_cout),
    .Z(csa8_8_z[7]), .Znext(csa8_8_znext));
  Register #(.width(7)) register_37 (.D(csa8_8_znext), .Q(register_37_q), .clk(clock_1_out));  // open: en, clr
  Register register_38 (.D({csa8_8_z[7], register_35_q}), .Q(Z[7:0]), .clk(clock_1_out));  // open: en, clr
  cpa cpa_1 (.A(register_36_q), .B(register_37_q), .Z(Z[15:8]), .Cout(Cout));
endmodule

module pipeline_mul8 (
  input  [7:0] A,
  input  [7:0] B,
  output [15:0] Z,
  output Cout
);

  wire clock_1_out;
  wire [3:0] csa8_1_z;
  wire [6:0] csa8_1_znext, csa8_2_znext, csa8_3_znext, csa8_4_znext, csa8_5_znext, csa8_6_znext,
       csa8_7_znext, csa8_8_znext, register_4_q, register_7_q;
  wire [7:0] csa8_1_cout, csa8_2_cout, csa8_3_cout, csa8_4_cout, csa8_5_cout, csa8_6_cout, csa8_7_cout,
       csa8_8_cout, register_1_q, register_2_q, register_3_q, register_5_q, register_6_q;

  Clock clock_1 (.out(clock_1_out));
  csa8 csa8_1 (
    .Cin({8{1'b0}}), .A(A), .B(B[0]), .C({7{1'b0}}), .Cout(csa8_1_cout), .Z(csa8_1_z[0]), .Znext(csa8_1_znext));
  csa8 csa8_2 (
    .Cin(csa8_1_cout), .A(A), .B(B[1]), .C(csa8_1_znext), .Cout(csa8_2_cout), .Z(csa8_1_z[1]),
    .Znext(csa8_2_znext));
  csa8 csa8_3 (
    .Cin(csa8_2_cout), .A(A), .B(B[2]), .C(csa8_2_znext), .Cout(csa8_3_cout), .Z(csa8_1_z[2]),
    .Znext(csa8_3_znext));
  Register register_1 (.D(A), .Q(register_1_q), .clk(clock_1_out));  // open: en, clr
  Register register_2 (.D(B), .Q(register_2_q), .clk(clock_1_out));  // open: en, clr
  Register register_3 (.D(csa8_4_cout), .Q(register_3_q), .clk(clock_1_out));  // open: en, clr
  csa8 csa8_4 (
    .Cin(csa8_3_cout), .A(A), .B(B[3]), .C(csa8_3_znext), .Cout(csa8_4_cout), .Z(csa8_1_z[3]),
    .Znext(csa8_4_znext));
  Register #(.width(7)) register_4 (.D(csa8_4_znext), .Q(register_4_q), .clk(clock_1_out));  // open: en, clr
  Register #(.width(4)) register_5 (.D(csa8_1_z), .Q(register_5_q[3:0]), .clk(clock_1_out));  // open: en, clr
  csa8 csa8_5 (
    .Cin(register_3_q), .A(register_1_q), .B(register_2_q[4]), .C(register_4_q), .Cout(csa8_5_cout),
    .Z(register_5_q[4]), .Znext(csa8_5_znext));
  csa8 csa8_6 (
    .Cin(csa8_5_cout), .A(register_1_q), .B(register_2_q[5]), .C(csa8_5_znext), .Cout(csa8_6_cout),
    .Z(register_5_q[5]), .Znext(csa8_6_znext));
  csa8 csa8_7 (
    .Cin(csa8_6_cout), .A(register_1_q), .B(register_2_q[6]), .C(csa8_6_znext), .Cout(csa8_7_cout),
    .Z(register_5_q[6]), .Znext(csa8_7_znext));
  Register register_6 (.D(csa8_8_cout), .Q(register_6_q), .clk(clock_1_out));  // open: en, clr
  csa8 csa8_8 (
    .Cin(csa8_7_cout), .A(register_1_q), .B(register_2_q[7]), .C(csa8_7_znext), .Cout(csa8_8_cout),
    .Z(register_5_q[7]), .Znext(csa8_8_znext));
  Register #(.width(7)) register_7 (.D(csa8_8_znext), .Q(register_7_q), .clk(clock_1_out));  // open: en, clr
  Register register_8 (.D(register_5_q), .Q(Z[7:0]), .clk(clock_1_out));  // open: en, clr
  cpa cpa_1 (.A(register_6_q), .B(register_7_q), .Z(Z[15:8]), .Cout(Cout));
endmodule
